// Logisim project cpu.circ as structural Verilog: 6 circuits, main circuit main
module main (
);

  wire adder_2_cout, and_1_out, and_2_out, and_3_out, CLK, comparator_1_eq, controller_1_writemem,
       controller_1_writereg, counter_1_carry, counter_4_carry, E, L, On, or_1_out, register_1_q, RST, sys;
  wire [0:0] controller_1_lb;
  wire [1:0] controller_1_aluymux, controller_1_rf1mux, controller_1_rf2mux, controller_1_rfdinmux,
       controller_1_wmux, PCMux;
  wire [2:0] \分支 ;
  wire [3:0] controller_1_aluop;
  wire [4:0] decode_1_rd, decode_1_rs, decode_1_rt, decode_1_sa, multiplexer_2_out, multiplexer_3_out,
       multiplexer_4_out;
  wire [5:0] decode_1_func, decode_1_op;
  wire [11:1] alu_1_result;
  wire [15:0] \总周期数 , \无条件分支指令数 , \有条件分支成功跳转 , \有条件分支指令数 ;
  wire [19:0] alu_1_result_2;
  wire [25:0] decode_1_address;
  wire [31:0] adder_1_out, adder_2_out, bit_extender_1_out, mips_ram_1_dataout, multiplexer_1_out,
       multiplexer_5_out, multiplexer_6_out, PC_q, registerfile_1_p7, rom_1_data, SyscallOut, v0;
  wire [31:16] decode_1_imm;

  Button \u_总复位  (.out(RST));
  Clock clock_1 (.out(CLK));
  Hex_Digit_Display hex_digit_display_1 (.value(SyscallOut[31:28]));  // open: dp
  Register #(.width(32)) PC (.D(multiplexer_5_out), .en(On), .Q(PC_q), .clk(CLK), .clr(RST));
  Hex_Digit_Display hex_digit_display_2 (.value(SyscallOut[27:24]));  // open: dp
  Hex_Digit_Display hex_digit_display_3 (.value(SyscallOut[23:20]));  // open: dp
  Adder #(.width(32)) adder_1 (.a(PC_q), .b(32'h4), .out(adder_1_out), .cin(1'b0));  // open: cout
  Counter #(.width(16), .max('hffff)) counter_1 (
    .load(1'b0), .D({16{1'b0}}), .count(\分支 [0]), .Q(\无条件分支指令数 ), .carry(counter_1_carry), .clk(CLK),
    .clr(RST));
  Hex_Digit_Display hex_digit_display_4 (.value(SyscallOut[15:12]));  // open: dp
  Hex_Digit_Display hex_digit_display_5 (.value(SyscallOut[19:16]));  // open: dp
  Hex_Digit_Display hex_digit_display_6 (.value(SyscallOut[11:8]));  // open: dp
  Hex_Digit_Display hex_digit_display_7 (.value(SyscallOut[7:4]));  // open: dp
  Comparator #(.width(32)) comparator_1 (.a(v0), .b(32'ha), .eq(comparator_1_eq));  // open: gt, lt
  Counter #(.width(16), .max('hffff)) counter_2 (
    .load(1'b0), .D({16{1'b0}}), .count(\分支 [1]), .Q(\有条件分支指令数 ), .clk(CLK), .clr(RST));  // open: carry
  Hex_Digit_Display hex_digit_display_8 (.value(SyscallOut[3:0]));  // open: dp
  nand nand_1 (On, comparator_1_eq, sys);
  DECODE decode_1 (
    .\指令 (rom_1_data), .rs(decode_1_rs), .rt(decode_1_rt), .rd(decode_1_rd), .func(decode_1_func),
    .Imm(decode_1_imm), .address(decode_1_address), .op(decode_1_op), .sa(decode_1_sa));
  ROM #(.addrWidth(10), .dataWidth(32)) rom_1 (.addr(PC_q[11:2]), .data(rom_1_data), .sel(1'b1));
  Multiplexer #(.select(2), .width(32), .enable("false")) multiplexer_1 (
    .in0({alu_1_result_2, alu_1_result, L}), .in1(mips_ram_1_dataout), .in2(adder_1_out),
    .in3({decode_1_imm, {16{1'b0}}}), .out(multiplexer_1_out), .sel(controller_1_rfdinmux));
  Controller controller_1 (
    .RfDinMux(controller_1_rfdinmux), .WriteReg(controller_1_writereg), .op(decode_1_op),
    .func(decode_1_func), .ALUop(controller_1_aluop), .WMux(controller_1_wmux), .PCMux(PCMux),
    .WriteMem(controller_1_writemem), .LB(controller_1_lb[0]), .SysCall(sys), .E(E), .L(L),
    .AluYMux(controller_1_aluymux), .RF1Mux(controller_1_rf1mux), .RF2Mux(controller_1_rf2mux),
    .\无条件分支 (\分支 [0]), .\有条件分支 (\分支 [1]), .\有条件分支成功 (\分支 [2]));
  Counter #(.width(16), .max('hffff)) counter_3 (
    .load(1'b0), .D({16{1'b0}}), .count(\分支 [2]), .Q(\有条件分支成功跳转 ), .clk(CLK), .clr(RST));  // open: carry
  // Probe on \总周期数 
  // Probe on \无条件分支指令数 
  // Probe on \有条件分支指令数 
  // Probe on \有条件分支成功跳转 
  and and_1 (and_1_out, On, controller_1_writereg);
  Multiplexer #(.select(2), .width(5), .disabled(0), .enable("false")) multiplexer_2 (
    .in0(decode_1_rd), .in1(decode_1_rt), .in2({5{1'b1}}), .in3({5{1'b0}}), .out(multiplexer_2_out),
    .sel(controller_1_wmux));
  Adder #(.width(32)) adder_2 (
    .a({{14{1'b0}}, decode_1_imm, 2'b00}), .b(adder_1_out), .out(adder_2_out), .cin(1'b0), .cout(adder_2_cout));
  Multiplexer #(.select(2), .width(5), .disabled(0), .enable("false")) multiplexer_3 (
    .in0(decode_1_rs), .in1(decode_1_rt), .in2(5'b00100), .in3(5'b00100), .out(multiplexer_3_out),
    .sel(controller_1_rf1mux));
  Multiplexer #(.select(2), .width(5), .disabled(0), .enable("false")) multiplexer_4 (
    .in0(decode_1_rt), .in1(decode_1_rs), .in2(5'b00010), .in3(5'b00010), .out(multiplexer_4_out),
    .sel(controller_1_rf2mux));
  Counter #(.width(16), .max('hffff)) counter_4 (
    .load(1'b0), .D({16{1'b0}}), .count(or_1_out), .Q(\总周期数 ), .carry(counter_4_carry), .clk(CLK), .clr(RST));
  or or_1 (or_1_out, On, register_1_q);
  Register #(.width(1)) register_1 (.D(On), .en(or_1_out), .Q(register_1_q), .clk(CLK), .clr(RST));
  // RegisterFile registerfile_1: pin names not known; wires that end beside it: multiplexer_1_out, CLK, and_1_out, multiplexer_2_out, multiplexer_3_out, multiplexer_4_out, registerfile_1_p7, v0
  assign bit_extender_1_out = {{16{decode_1_imm[31]}}, decode_1_imm};  // Bit_Extender bit_extender_1
  and and_2 (and_2_out, sys, On);
  Multiplexer #(.select(2), .width(32), .disabled(0), .enable("false")) multiplexer_5 (
    .in0(adder_1_out), .in1(adder_2_out), .in2({adder_1_out[31:28], decode_1_address, 2'b00}),
    .in3(registerfile_1_p7), .out(multiplexer_5_out), .sel(PCMux));
  Register #(.width(32)) register_2 (.D(registerfile_1_p7), .en(and_2_out), .Q(SyscallOut), .clk(CLK), .clr(RST));
  ALU alu_1 (
    .AluOP(controller_1_aluop), .X(registerfile_1_p7), .Equal(E), .Result({alu_1_result_2, alu_1_result, L}),
    .Y(multiplexer_6_out));  // open: Signed_Overflow, Result_2, UnSigned_Overflow
  Multiplexer #(.select(2), .width(32), .disabled(0), .enable("false")) multiplexer_6 (
    .in0(v0), .in1(bit_extender_1_out), .in2({{16{1'b0}}, decode_1_imm}), .in3({{27{1'b0}}, decode_1_sa}),
    .out(multiplexer_6_out), .sel(controller_1_aluymux));
  MIPS_RAM mips_ram_1 (
    .\字节地址 ({alu_1_result, L}), .Din(v0), .DataOut(mips_ram_1_dataout), .CLK(CLK), .WR(and_3_out),
    .Mode({1'b0, controller_1_lb[0]}), .RST(RST));
  and and_3 (and_3_out, On, controller_1_writemem);

  // Notes on the sheet:
  //   数码管输出应该用寄存器锁存，否则显示数据只能一闪而过
  //   可以通过项目增加Logisim库的方式将前几次实验完成的电路作为子电路引入到本电路中使用
  //   数码管输出
  //   contents of rom_1 (hex, n*v repeats v):
  //   20080000 3c010403 20290201 92021 20020022 c ad090000 81110000 81120001 81130002 81140003 112021
  //   20020022 c 122021 20020022 c 132021 20020022 c 142021 20020022 c 2108fff6 21080001 1900fffe 20080004
  //   1129004 2518025 20080008 1139804 2138025 2008000c 114a004 2148025 102021 20020022 c 2002000a c
  //   总复位信号应将除ROM以外所有存储组件全部清零
endmodule

module DECODE (
  input  [31:0] \指令 ,
  output [15:0] Imm,
  output [5:0] func,
  output [25:0] address,
  output [4:0] sa,
  output [4:0] rd,
  output [4:0] rt,
  output [5:0] op,
  output [4:0] rs
);


  assign address = \指令 [25:0];
  assign func = \指令 [5:0];
  assign Imm = \指令 [15:0];
  assign op = \指令 [31:26];
  assign rd = \指令 [15:11];
  assign rs = \指令 [25:21];
  assign rt = \指令 [20:16];
  assign sa = \指令 [10:6];
endmodule

module Controller (
  input  E,
  input  L,
  input  [5:0] op,
  input  [5:0] func,
  output [1:0] WMux,
  output [1:0] RF1Mux,
  output [1:0] RfDinMux,
  output [1:0] RF2Mux,
  output [1:0] PCMux,
  output [1:0] AluYMux,
  output WriteReg,
  output WriteMem,
  output \有条件分支成功 ,
  output LB,
  output SysCall,
  output \有条件分支 ,
  output \无条件分支 ,
  output [3:0] ALUop
);

  wire and_1_out, and_2_out, and_3_out, Beq, BLEZ, Bne, Imm, ImmBit, J, JR, Load, LUI, or_3_out, Shift;

  or or_1 (RfDinMux[1], LUI, WMux[1]);
  or or_2 (RfDinMux[0], LUI, Load);
  test1 test1_1 (
    .op5(op[5]), .op4(op[4]), .op3(op[3]), .op2(op[2]), .op1(op[1]), .op0(op[0]), .fun5(func[5]),
    .fun4(func[4]), .Imm(Imm), .fun3(func[3]), .fun2(func[2]), .fun1(func[1]), .fun0(func[0]),
    .ImmBit(ImmBit), .LB(LB), .SysCall(RF1Mux[1]), .alu3(ALUop[3]), .alu2(ALUop[2]), .alu1(ALUop[1]),
    .alu0(ALUop[0]), .Sllv(RF2Mux[0]));
  and and_1 (and_1_out, Beq, E);
  and and_2 (and_2_out, ~E, Bne);  // AND_Gate
  or or_3 (or_3_out, E, L);
  and and_3 (and_3_out, or_3_out, BLEZ);
  test test_1 (
    .op5(op[5]), .op4(op[4]), .op3(op[3]), .op2(op[2]), .op1(op[1]), .op0(op[0]), .fun5(func[5]),
    .fun4(func[4]), .fun3(func[3]), .WriteReg(WriteReg), .fun2(func[2]), .fun1(func[1]), .fun0(func[0]),
    .WriteMem(WriteMem), .Beq(Beq), .Bne(Bne), .BLEZ(BLEZ), .J(J), .JR(JR), .RegShift(Shift),
    .Iwrite(WMux[0]), .Link(WMux[1]), .Load(Load), .LUI(LUI));
  or or_4 (\有条件分支成功 , and_1_out, and_2_out, and_3_out);
  or or_5 (PCMux[1], JR, J);
  or or_6 (PCMux[0], JR, \有条件分支成功 );
  or or_7 (\无条件分支 , J, JR);
  or or_8 (RF1Mux[0], RF2Mux[0], Shift);
  or or_9 (AluYMux[1], Shift, ImmBit);
  or or_10 (AluYMux[0], Shift, Imm);
  or or_11 (\有条件分支 , Beq, Bne, BLEZ);

  assign RF2Mux[1] = RF1Mux[1];
  assign SysCall = RF1Mux[1];

  // Other names for the same wires on the sheet: funcT[5:0] = func; opT[5:0] = op; Sllv = RF2Mux[0]; Iwrite = WMux[0];
  //   Link = WMux[1]
endmodule

module test (
  input  op5,
  input  op4,
  input  op3,
  input  op2,
  input  op1,
  input  op0,
  input  fun5,
  input  fun4,
  input  fun3,
  input  fun2,
  input  fun1,
  input  fun0,
  output WriteReg,
  output WriteMem,
  output Beq,
  output Bne,
  output BLEZ,
  output J,
  output JR,
  output RegShift,
  output Iwrite,
  output Link,
  output Load,
  output LUI
);

  wire and_1_out, and_2_out, and_3_out, and_4_out, and_5_out, and_6_out, and_7_out, and_14_out, and_15_out,
       and_16_out, and_17_out, and_18_out, and_19_out, and_20_out, and_21_out, and_22_out, and_23_out,
       and_25_out, and_26_out, not_1_out, not_2_out, not_3_out, not_4_out, not_5_out, not_6_out, not_7_out,
       not_8_out, not_9_out, not_10_out, not_11_out, not_12_out, not_13_out, not_14_out, not_15_out,
       not_16_out, not_17_out, not_18_out, not_19_out, not_20_out, not_21_out, not_22_out, not_23_out,
       not_24_out, not_25_out, not_26_out, not_27_out, not_28_out, not_29_out, not_30_out, not_31_out,
       not_32_out, not_33_out, not_34_out, not_35_out, not_36_out, not_37_out, not_38_out, not_39_out,
       not_40_out, not_41_out, not_42_out, not_43_out, not_44_out, not_45_out, not_46_out, not_47_out,
       not_48_out, not_49_out, not_50_out, not_51_out, not_52_out, not_53_out, not_54_out, not_55_out,
       not_56_out, not_57_out, not_58_out, not_59_out, not_60_out, not_61_out, not_62_out, not_63_out,
       not_64_out, not_65_out, not_66_out, not_67_out, not_68_out, not_69_out, not_70_out, not_71_out,
       not_72_out, not_73_out, not_74_out, not_75_out, not_76_out, not_77_out, not_78_out, not_79_out,
       not_80_out, not_81_out, not_82_out, not_83_out, not_84_out, not_85_out, not_86_out, not_87_out,
       not_88_out, not_89_out, not_90_out, not_91_out, not_92_out, not_93_out, not_94_out, not_95_out,
       not_96_out, not_97_out, not_98_out, not_99_out, not_100_out, not_101_out, not_102_out, not_103_out,
       not_104_out, not_105_out, not_106_out, not_107_out, not_108_out, not_109_out, not_110_out,
       not_111_out, not_112_out, not_113_out, not_114_out, not_115_out, not_116_out, not_117_out,
       not_118_out, not_119_out, not_120_out, not_121_out, not_122_out, not_123_out, not_124_out,
       not_125_out, not_126_out, not_127_out, not_128_out, not_129_out, not_130_out, not_131_out, or_1_out;

  not not_1 (not_1_out, op4);
  not not_2 (not_2_out, op2);
  not not_3 (not_3_out, op5);
  not not_4 (not_4_out, op4);
  not not_5 (not_5_out, op3);
  not not_6 (not_6_out, op1);
  not not_7 (not_7_out, op0);
  not not_8 (not_8_out, op5);
  not not_9 (not_9_out, op4);
  not not_10 (not_10_out, op3);
  not not_11 (not_11_out, op1);
  not not_12 (not_12_out, op5);
  not not_13 (not_13_out, op4);
  not not_14 (not_14_out, op3);
  not not_15 (not_15_out, op2);
  not not_16 (not_16_out, op0);
  not not_17 (not_17_out, op5);
  not not_18 (not_18_out, op4);
  not not_19 (not_19_out, op3);
  not not_20 (not_20_out, op0);
  not not_21 (not_21_out, op5);
  not not_22 (not_22_out, op4);
  not not_23 (not_23_out, op3);
  not not_24 (not_24_out, op2);
  not not_25 (not_25_out, op1);
  not not_26 (not_26_out, op0);
  not not_27 (not_27_out, fun5);
  not not_28 (not_28_out, fun4);
  not not_29 (not_29_out, fun2);
  not not_30 (not_30_out, fun1);
  not not_31 (not_31_out, fun0);
  not not_32 (not_32_out, op5);
  not not_33 (not_33_out, op4);
  not not_34 (not_34_out, op3);
  not not_35 (not_35_out, op2);
  not not_36 (not_36_out, op1);
  not not_37 (not_37_out, op0);
  not not_38 (not_38_out, fun5);
  not not_39 (not_39_out, fun4);
  not not_40 (not_40_out, fun1);
  not not_41 (not_41_out, fun0);
  not not_42 (not_42_out, op4);
  not not_43 (not_43_out, op2);
  not not_44 (not_44_out, op5);
  not not_45 (not_45_out, op4);
  not not_46 (not_46_out, op3);
  not not_47 (not_47_out, op1);
  not not_48 (not_48_out, op0);
  not not_49 (not_49_out, op5);
  not not_50 (not_50_out, op4);
  not not_51 (not_51_out, op3);
  not not_52 (not_52_out, op1);
  not not_53 (not_53_out, op5);
  not not_54 (not_54_out, op4);
  not not_55 (not_55_out, op3);
  not not_56 (not_56_out, op0);
  not not_57 (not_57_out, op5);
  not not_58 (not_58_out, op4);
  not not_59 (not_59_out, op3);
  not not_60 (not_60_out, op2);
  not not_61 (not_61_out, op5);
  not not_62 (not_62_out, op4);
  not not_63 (not_63_out, op3);
  not not_64 (not_64_out, op2);
  not not_65 (not_65_out, op1);
  not not_66 (not_66_out, op0);
  not not_67 (not_67_out, fun5);
  not not_68 (not_68_out, fun4);
  not not_69 (not_69_out, fun2);
  not not_70 (not_70_out, fun1);
  not not_71 (not_71_out, fun0);
  not not_72 (not_72_out, fun5);
  not not_73 (not_73_out, fun4);
  not not_74 (not_74_out, fun3);
  not not_75 (not_75_out, fun2);
  not not_76 (not_76_out, fun5);
  not not_77 (not_77_out, fun4);
  not not_78 (not_78_out, fun3);
  not not_79 (not_79_out, fun2);
  not not_80 (not_80_out, fun1);
  not not_81 (not_81_out, fun0);
  not not_82 (not_82_out, op5);
  not not_83 (not_83_out, op4);
  not not_84 (not_84_out, op2);
  not not_85 (not_85_out, op1);
  not not_86 (not_86_out, op0);
  not not_87 (not_87_out, op5);
  not not_88 (not_88_out, op4);
  not not_89 (not_89_out, op2);
  not not_90 (not_90_out, op1);
  not not_91 (not_91_out, op5);
  not not_92 (not_92_out, op4);
  not not_93 (not_93_out, op1);
  not not_94 (not_94_out, op0);
  not not_95 (not_95_out, op5);
  not not_96 (not_96_out, op4);
  not not_97 (not_97_out, op1);
  not not_98 (not_98_out, op4);
  not not_99 (not_99_out, op3);
  not not_100 (not_100_out, op2);
  not not_101 (not_101_out, op5);
  not not_102 (not_102_out, op4);
  not not_103 (not_103_out, op2);
  not not_104 (not_104_out, op0);
  not not_105 (not_105_out, op5);
  not not_106 (not_106_out, op4);
  not not_107 (not_107_out, op4);
  not not_108 (not_108_out, op3);
  not not_109 (not_109_out, op2);
  not not_110 (not_110_out, op1);
  not not_111 (not_111_out, op0);
  not not_112 (not_112_out, op5);
  not not_113 (not_113_out, op4);
  not not_114 (not_114_out, op3);
  not not_115 (not_115_out, op2);
  not not_116 (not_116_out, op4);
  not not_117 (not_117_out, op3);
  not not_118 (not_118_out, op2);
  not not_119 (not_119_out, op4);
  not not_120 (not_120_out, op3);
  not not_121 (not_121_out, op2);
  not not_122 (not_122_out, op1);
  not not_123 (not_123_out, op0);
  not not_124 (not_124_out, op5);
  not not_125 (not_125_out, op4);
  and and_1 (and_1_out, op5, not_1_out, op3, not_2_out, op1, op0);
  and and_2 (and_2_out, not_3_out, not_4_out, not_5_out, op2, not_6_out, not_7_out);
  and and_3 (and_3_out, not_8_out, not_9_out, not_10_out, op2, not_11_out, op0);
  and and_4 (and_4_out, not_12_out, not_13_out, not_14_out, not_15_out, op1, not_16_out);
  and and_5 (and_5_out, not_17_out, not_18_out, not_19_out, op2, op1, not_20_out);
  and and_6 (and_6_out, not_21_out, not_22_out, not_23_out, not_24_out, not_25_out, not_26_out, not_27_out, not_28_out, fun3, not_29_out, not_30_out, not_31_out);
  and and_7 (and_7_out, not_32_out, not_33_out, not_34_out, not_35_out, not_36_out, not_37_out, not_38_out, not_39_out, fun3, fun2, not_40_out, not_41_out);
  and and_8 (WriteMem, op5, not_42_out, op3, not_43_out, op1, op0);
  and and_9 (Beq, not_44_out, not_45_out, not_46_out, op2, not_47_out, not_48_out);
  and and_10 (Bne, not_49_out, not_50_out, not_51_out, op2, not_52_out, op0);
  and and_11 (BLEZ, not_53_out, not_54_out, not_55_out, op2, op1, not_56_out);
  and and_12 (J, not_57_out, not_58_out, not_59_out, not_60_out, op1);
  and and_13 (JR, not_61_out, not_62_out, not_63_out, not_64_out, not_65_out, not_66_out, not_67_out, not_68_out, fun3, not_69_out, not_70_out, not_71_out);
  and and_14 (and_14_out, not_72_out, not_73_out, not_74_out, not_75_out, fun1);
  and and_15 (and_15_out, not_76_out, not_77_out, not_78_out, not_79_out, not_80_out, not_81_out);
  and and_16 (and_16_out, not_82_out, not_83_out, op3, not_84_out, not_85_out, not_86_out);
  and and_17 (and_17_out, not_87_out, not_88_out, op3, not_89_out, not_90_out, op0);
  and and_18 (and_18_out, not_91_out, not_92_out, op3, op2, not_93_out, not_94_out);
  and and_19 (and_19_out, not_95_out, not_96_out, op3, op2, not_97_out, op0);
  and and_20 (and_20_out, op5, not_98_out, not_99_out, not_100_out, op1, op0);
  and and_21 (and_21_out, not_101_out, not_102_out, op3, not_103_out, op1, not_104_out);
  and and_22 (and_22_out, not_105_out, not_106_out, op3, op2, op1, op0);
  and and_23 (and_23_out, op5, not_107_out, not_108_out, not_109_out, not_110_out, not_111_out);
  and and_24 (Link, not_112_out, not_113_out, not_114_out, not_115_out, op1, op0);
  and and_25 (and_25_out, op5, not_116_out, not_117_out, not_118_out, op1, op0);
  and and_26 (and_26_out, op5, not_119_out, not_120_out, not_121_out, not_122_out, not_123_out);
  and and_27 (LUI, not_124_out, not_125_out, op3, op2, op1, op0);
  nor nor_1 (WriteReg, and_1_out, and_2_out, and_3_out, and_4_out, and_5_out, and_6_out, and_7_out);
  not not_126 (not_126_out, op5);
  not not_127 (not_127_out, op4);
  not not_128 (not_128_out, op3);
  not not_129 (not_129_out, op2);
  not not_130 (not_130_out, op1);
  not not_131 (not_131_out, op0);
  or or_1 (or_1_out, and_14_out, and_15_out);
  or or_2 (Iwrite, and_16_out, and_17_out, and_18_out, and_19_out, and_20_out, and_21_out, and_22_out, and_23_out);
  or or_3 (Load, and_25_out, and_26_out);
  and and_28 (RegShift, not_126_out, not_127_out, not_128_out, not_129_out, not_130_out, not_131_out, or_1_out);
endmodule

module test1 (
  input  op5,
  input  op4,
  input  op3,
  input  op2,
  input  op1,
  input  op0,
  input  fun5,
  input  fun4,
  input  fun3,
  input  fun2,
  input  fun1,
  input  fun0,
  output Imm,
  output ImmBit,
  output LB,
  output SysCall,
  output alu3,
  output alu2,
  output alu1,
  output alu0,
  output Sllv
);

  wire and_1_out, and_2_out, and_3_out, and_4_out, and_5_out, and_6_out, and_10_out, and_11_out, and_12_out,
       and_13_out, and_14_out, and_15_out, and_16_out, and_17_out, and_18_out, and_19_out, and_20_out,
       and_21_out, and_22_out, and_23_out, and_24_out, and_26_out, and_27_out, and_28_out, and_29_out,
       and_30_out, and_31_out, and_32_out, and_33_out, and_34_out, and_35_out, and_36_out, and_37_out,
       and_38_out, and_39_out, and_40_out, not_1_out, not_2_out, not_3_out, not_4_out, not_5_out, not_6_out,
       not_7_out, not_8_out, not_9_out, not_10_out, not_11_out, not_12_out, not_13_out, not_14_out,
       not_15_out, not_16_out, not_17_out, not_18_out, not_19_out, not_20_out, not_21_out, not_22_out,
       not_23_out, not_24_out, not_25_out, not_26_out, not_27_out, not_28_out, not_29_out, not_30_out,
       not_31_out, not_32_out, not_33_out, not_34_out, not_35_out, not_36_out, not_37_out, not_38_out,
       not_39_out, not_40_out, not_41_out, not_42_out, not_43_out, not_44_out, not_45_out, not_46_out,
       not_47_out, not_48_out, not_49_out, not_50_out, not_51_out, not_52_out, not_53_out, not_54_out,
       not_55_out, not_56_out, not_57_out, not_58_out, not_59_out, not_60_out, not_61_out, not_62_out,
       not_63_out, not_64_out, not_65_out, not_66_out, not_67_out, not_68_out, not_69_out, not_70_out,
       not_71_out, not_72_out, not_73_out, not_74_out, not_75_out, not_76_out, not_77_out, not_78_out,
       not_79_out, not_80_out, not_81_out, not_82_out, not_83_out, not_84_out, not_85_out, not_86_out,
       not_87_out, not_88_out, not_89_out, not_90_out, not_91_out, not_92_out, not_93_out, not_94_out,
       not_95_out, not_96_out, not_97_out, not_98_out, not_99_out, not_100_out, not_101_out, not_102_out,
       not_103_out, not_104_out, not_105_out, not_106_out, not_107_out, not_108_out, not_109_out,
       not_110_out, not_111_out, not_112_out, not_113_out, not_114_out, not_115_out, not_116_out,
       not_117_out, not_118_out, not_119_out, not_120_out, not_121_out, not_122_out, not_123_out,
       not_124_out, not_125_out, not_126_out, not_127_out, not_128_out, not_129_out, not_130_out,
       not_131_out, not_132_out, not_133_out, not_134_out, not_135_out, not_136_out, not_137_out,
       not_138_out, not_139_out, not_140_out, not_141_out, not_142_out, not_143_out, not_144_out,
       not_145_out, not_146_out, not_147_out, not_148_out, not_149_out, not_150_out, not_151_out,
       not_152_out, not_153_out, not_154_out, not_155_out, not_156_out, not_157_out, not_158_out,
       not_159_out, not_160_out, not_161_out, not_162_out, not_163_out, not_164_out, not_165_out,
       not_166_out, not_167_out, not_168_out, not_169_out, or_1_out, or_3_out, or_4_out, or_5_out;

  not not_1 (not_1_out, op5);
  not not_2 (not_2_out, op4);
  not not_3 (not_3_out, op2);
  not not_4 (not_4_out, op1);
  not not_5 (not_5_out, op5);
  not not_6 (not_6_out, op4);
  not not_7 (not_7_out, op2);
  not not_8 (not_8_out, op1);
  not not_9 (not_9_out, op0);
  not not_10 (not_10_out, op4);
  not not_11 (not_11_out, op3);
  not not_12 (not_12_out, op2);
  not not_13 (not_13_out, op4);
  not not_14 (not_14_out, op2);
  not not_15 (not_15_out, op5);
  not not_16 (not_16_out, op4);
  not not_17 (not_17_out, op2);
  not not_18 (not_18_out, op0);
  not not_19 (not_19_out, op4);
  not not_20 (not_20_out, op3);
  not not_21 (not_21_out, op2);
  not not_22 (not_22_out, op1);
  not not_23 (not_23_out, op0);
  not not_24 (not_24_out, op5);
  not not_25 (not_25_out, op4);
  not not_26 (not_26_out, op1);
  not not_27 (not_27_out, op4);
  not not_28 (not_28_out, op3);
  not not_29 (not_29_out, op2);
  not not_30 (not_30_out, op1);
  not not_31 (not_31_out, op0);
  not not_32 (not_32_out, op5);
  not not_33 (not_33_out, op4);
  not not_34 (not_34_out, op3);
  not not_35 (not_35_out, op2);
  not not_36 (not_36_out, op1);
  not not_37 (not_37_out, op0);
  not not_38 (not_38_out, fun5);
  not not_39 (not_39_out, fun4);
  not not_40 (not_40_out, fun1);
  not not_41 (not_41_out, fun0);
  not not_42 (not_42_out, fun4);
  not not_43 (not_43_out, fun3);
  not not_44 (not_44_out, fun4);
  not not_45 (not_45_out, fun2);
  not not_46 (not_46_out, fun5);
  not not_47 (not_47_out, fun4);
  not not_48 (not_48_out, fun3);
  not not_49 (not_49_out, fun1);
  not not_50 (not_50_out, fun0);
  not not_51 (not_51_out, fun5);
  not not_52 (not_52_out, fun4);
  not not_53 (not_53_out, fun3);
  not not_54 (not_54_out, fun2);
  not not_55 (not_55_out, fun4);
  not not_56 (not_56_out, fun3);
  not not_57 (not_57_out, fun4);
  not not_58 (not_58_out, fun2);
  not not_59 (not_59_out, fun0);
  not not_60 (not_60_out, fun4);
  not not_61 (not_61_out, fun3);
  not not_62 (not_62_out, fun2);
  not not_63 (not_63_out, fun0);
  not not_64 (not_64_out, fun4);
  not not_65 (not_65_out, fun3);
  not not_66 (not_66_out, fun1);
  not not_67 (not_67_out, fun0);
  not not_68 (not_68_out, fun4);
  not not_69 (not_69_out, fun2);
  not not_70 (not_70_out, fun0);
  not not_71 (not_71_out, fun4);
  not not_72 (not_72_out, fun3);
  not not_73 (not_73_out, fun5);
  not not_74 (not_74_out, fun4);
  not not_75 (not_75_out, fun3);
  not not_76 (not_76_out, fun1);
  not not_77 (not_77_out, fun0);
  not not_78 (not_78_out, fun4);
  not not_79 (not_79_out, fun3);
  not not_80 (not_80_out, fun2);
  not not_81 (not_81_out, fun0);
  not not_82 (not_82_out, fun4);
  not not_83 (not_83_out, fun3);
  not not_84 (not_84_out, fun1);
  not not_85 (not_85_out, fun4);
  not not_86 (not_86_out, fun2);
  not not_87 (not_87_out, fun4);
  not not_88 (not_88_out, fun3);
  not not_89 (not_89_out, op5);
  not not_90 (not_90_out, op4);
  not not_91 (not_91_out, op3);
  not not_92 (not_92_out, op2);
  not not_93 (not_93_out, op1);
  not not_94 (not_94_out, op0);
  not not_95 (not_95_out, fun5);
  not not_96 (not_96_out, fun4);
  not not_97 (not_97_out, fun3);
  not not_98 (not_98_out, fun1);
  not not_99 (not_99_out, fun0);
  and and_1 (and_1_out, not_1_out, not_2_out, op3, not_3_out, not_4_out, op0);
  and and_2 (and_2_out, not_5_out, not_6_out, op3, not_7_out, not_8_out, not_9_out);
  and and_3 (and_3_out, op5, not_10_out, not_11_out, not_12_out, op1, op0);
  and and_4 (and_4_out, op5, not_13_out, op3, not_14_out, op1, op0);
  and and_5 (and_5_out, not_15_out, not_16_out, op3, not_17_out, op1, not_18_out);
  and and_6 (and_6_out, op5, not_19_out, not_20_out, not_21_out, not_22_out, not_23_out);
  and and_7 (ImmBit, not_24_out, not_25_out, op3, op2, not_26_out);
  and and_8 (LB, op5, not_27_out, not_28_out, not_29_out, not_30_out, not_31_out);
  and and_9 (SysCall, not_32_out, not_33_out, not_34_out, not_35_out, not_36_out, not_37_out, not_38_out, not_39_out, fun3, fun2, not_40_out, not_41_out);
  not not_100 (not_100_out, op5);
  not not_101 (not_101_out, op4);
  not not_102 (not_102_out, op3);
  not not_103 (not_103_out, op2);
  not not_104 (not_104_out, op1);
  not not_105 (not_105_out, op0);
  not not_106 (not_106_out, fun4);
  not not_107 (not_107_out, fun3);
  not not_108 (not_108_out, fun1);
  not not_109 (not_109_out, op5);
  not not_110 (not_110_out, op4);
  not not_111 (not_111_out, op3);
  not not_112 (not_112_out, op2);
  not not_113 (not_113_out, op1);
  not not_114 (not_114_out, op0);
  and and_10 (and_10_out, not_42_out, not_43_out, fun2, fun1, fun0);
  or or_1 (or_1_out, and_10_out, and_11_out);
  and and_11 (and_11_out, fun5, not_44_out, fun3, not_45_out, fun1);
  and and_12 (and_12_out, not_46_out, not_47_out, not_48_out, not_49_out, not_50_out);
  and and_13 (and_13_out, not_51_out, not_52_out, not_53_out, not_54_out, fun1);
  and and_14 (and_14_out, fun5, not_55_out, not_56_out, fun2, fun0);
  and and_15 (and_15_out, fun5, not_57_out, fun3, not_58_out, fun1, not_59_out);
  and and_16 (and_16_out, not_60_out, not_61_out, not_62_out, fun1, not_63_out);
  and and_17 (and_17_out, fun5, not_64_out, not_65_out, fun2, not_66_out, not_67_out);
  and and_18 (and_18_out, fun5, not_68_out, fun3, not_69_out, fun1, not_70_out);
  and and_19 (and_19_out, fun5, not_71_out, not_72_out, fun2, fun1, fun0);
  and and_20 (and_20_out, not_73_out, not_74_out, not_75_out, not_76_out, not_77_out);
  and and_21 (and_21_out, not_78_out, not_79_out, not_80_out, fun1, not_81_out);
  and and_22 (and_22_out, fun5, not_82_out, not_83_out, fun2, not_84_out, fun0);
  and and_23 (and_23_out, fun5, not_85_out, fun3, not_86_out, fun1, fun0);
  and and_24 (and_24_out, fun5, not_87_out, not_88_out, fun2, fun1, fun0);
  and and_25 (Sllv, not_89_out, not_90_out, not_91_out, not_92_out, not_93_out, not_94_out, not_95_out, not_96_out, not_97_out, fun2, not_98_out, not_99_out);
  or or_2 (Imm, and_1_out, and_2_out, and_3_out, and_4_out, and_5_out, and_6_out);
  not not_115 (not_115_out, op5);
  not not_116 (not_116_out, op4);
  not not_117 (not_117_out, op1);
  not not_118 (not_118_out, op5);
  not not_119 (not_119_out, op4);
  not not_120 (not_120_out, op2);
  not not_121 (not_121_out, op0);
  not not_122 (not_122_out, op5);
  not not_123 (not_123_out, op4);
  not not_124 (not_124_out, op3);
  not not_125 (not_125_out, op0);
  not not_126 (not_126_out, op5);
  not not_127 (not_127_out, op4);
  not not_128 (not_128_out, op1);
  not not_129 (not_129_out, op5);
  not not_130 (not_130_out, op4);
  not not_131 (not_131_out, op2);
  not not_132 (not_132_out, op0);
  not not_133 (not_133_out, op5);
  not not_134 (not_134_out, op4);
  not not_135 (not_135_out, op3);
  not not_136 (not_136_out, op0);
  not not_137 (not_137_out, op5);
  not not_138 (not_138_out, op4);
  not not_139 (not_139_out, op3);
  not not_140 (not_140_out, op2);
  not not_141 (not_141_out, op1);
  not not_142 (not_142_out, op0);
  or or_3 (or_3_out, and_12_out, and_13_out, and_14_out, and_15_out);
  not not_143 (not_143_out, op5);
  not not_144 (not_144_out, op4);
  not not_145 (not_145_out, op3);
  not not_146 (not_146_out, op2);
  not not_147 (not_147_out, op1);
  not not_148 (not_148_out, op0);
  or or_4 (or_4_out, and_16_out, and_17_out, and_18_out, and_19_out);
  not not_149 (not_149_out, op5);
  not not_150 (not_150_out, op4);
  not not_151 (not_151_out, op1);
  not not_152 (not_152_out, op0);
  not not_153 (not_153_out, op5);
  not not_154 (not_154_out, op4);
  not not_155 (not_155_out, op2);
  not not_156 (not_156_out, op0);
  not not_157 (not_157_out, op5);
  not not_158 (not_158_out, op4);
  not not_159 (not_159_out, op3);
  not not_160 (not_160_out, op0);
  not not_161 (not_161_out, op5);
  not not_162 (not_162_out, op4);
  not not_163 (not_163_out, op3);
  not not_164 (not_164_out, op2);
  not not_165 (not_165_out, op1);
  not not_166 (not_166_out, op0);
  or or_5 (or_5_out, and_20_out, and_21_out, and_22_out, and_23_out, and_24_out);
  not not_167 (not_167_out, op5);
  not not_168 (not_168_out, op4);
  not not_169 (not_169_out, op1);
  and and_26 (and_26_out, not_100_out, not_101_out, not_102_out, not_103_out, not_104_out, not_105_out, fun5, not_106_out, not_107_out, fun2, not_108_out, fun0);
  and and_27 (and_27_out, not_115_out, not_116_out, op3, op2, not_117_out, op0);
  and and_28 (and_28_out, not_109_out, not_110_out, not_111_out, not_112_out, not_113_out, not_114_out, fun5, or_1_out);
  and and_29 (and_29_out, not_118_out, not_119_out, op3, not_120_out, op1, not_121_out);
  and and_30 (and_30_out, not_122_out, not_123_out, not_124_out, op2, op1, not_125_out);
  and and_31 (and_31_out, not_126_out, not_127_out, op3, op2, not_128_out, op0);
  and and_32 (and_32_out, not_129_out, not_130_out, op3, not_131_out, op1, not_132_out);
  and and_33 (and_33_out, not_133_out, not_134_out, not_135_out, op2, op1, not_136_out);
  and and_34 (and_34_out, not_137_out, not_138_out, not_139_out, not_140_out, not_141_out, not_142_out, or_3_out);
  and and_35 (and_35_out, not_143_out, not_144_out, not_145_out, not_146_out, not_147_out, not_148_out, or_4_out);
  and and_36 (and_36_out, not_149_out, not_150_out, op3, op2, not_151_out, not_152_out);
  and and_37 (and_37_out, not_153_out, not_154_out, op3, not_155_out, op1, not_156_out);
  and and_38 (and_38_out, not_157_out, not_158_out, not_159_out, op2, op1, not_160_out);
  and and_39 (and_39_out, not_161_out, not_162_out, not_163_out, not_164_out, not_165_out, not_166_out, or_5_out);
  and and_40 (and_40_out, not_167_out, not_168_out, op3, op2, not_169_out, op0);
  or or_6 (alu3, and_26_out, and_27_out, and_28_out, and_29_out, and_30_out);
  nor nor_1 (alu2, and_31_out, and_32_out, and_33_out, and_34_out);
  or or_7 (alu1, and_35_out, and_36_out, and_37_out, and_38_out);
  nor nor_2 (alu0, and_39_out, and_40_out);
endmodule

module q (
  input  word,
  input  half,
  input  half_sel,
  input  \byte ,
  input  byte_sel,
  output sel_3,
  output sel_2,
  output sel_1,
  output sel_0
);

  wire and_1_out, and_2_out, and_3_out, and_4_out, and_5_out, and_6_out, and_7_out, and_8_out, not_1_out,
       not_2_out;

  and and_1 (and_1_out, half, half_sel);
  and and_2 (and_2_out, half_sel, \byte , byte_sel);
  and and_3 (and_3_out, half, half_sel);
  and and_4 (and_4_out, half_sel, \byte , ~byte_sel);  // AND_Gate
  and and_5 (and_5_out, half, not_1_out);
  not not_1 (not_1_out, half_sel);
  and and_6 (and_6_out, not_1_out, \byte , byte_sel);
  and and_7 (and_7_out, half, not_2_out);
  not not_2 (not_2_out, half_sel);
  and and_8 (and_8_out, not_2_out, \byte , ~byte_sel);  // AND_Gate
  or or_1 (sel_3, word, and_1_out, and_2_out);
  or or_2 (sel_2, word, and_3_out, and_4_out);
  or or_3 (sel_1, word, and_5_out, and_6_out);
  or or_4 (sel_0, word, and_7_out, and_8_out);
endmodule
